# Fritzing sketch Lys fritz (saved by Fritzing 0.9.9b)
perfboards: 2

parts:
  Q1 = PNP-Transistor [package="TO92 [THT]"]
  R2 = Resistor [tolerance=±5% resistance=1.6k package="1206 [SMD]"]
  R3 = Resistor [tolerance=±5% resistance=120 package="1206 [SMD]"]
  R4 = Resistor [tolerance=±5% resistance=220 package="1206 [SMD]"]
  R5 = Resistor [tolerance=±5% resistance=220 package="1206 [SMD]"]
  D1 = Diode [package=diode-1n4001]  # not connected
  D2 = Diode [package=diode-1n4001]
  JP1 = Header 1 [package=1x01_offset]
  JP2 = Header 1 [package=1x01_offset]
  JP3 = Header 1 [package=1x01_offset]
  JP4 = Header 1 [package=1x01_offset]
  JP5 = Header 1 [package=1x01_offset]  # not connected
  JP6 = Header 1 [package=1x01_offset]
  JP7 = Header 1 [package=1x01_offset]  # not connected
  Q2 = PNP-Transistor [package="TO92 [THT]"]  # not connected
  R6 = Resistor [tolerance=±5% resistance=1.6k package="1206 [SMD]"]
  R7 = Resistor [tolerance=±5% resistance=120 package="1206 [SMD]"]
  R8 = Resistor [tolerance=±5% resistance=220 package="1206 [SMD]"]
  R9 = Resistor [tolerance=±5% resistance=220 package="1206 [SMD]"]
  D3 = Diode [package=diode-1n4001]  # not connected
  D4 = Diode [package=diode-1n4001]
  JP8 = Header 1 [package=1x01_offset]  # not connected
  JP9 = Header 1 [package=1x01_offset]  # not connected
  JP10 = Header 1 [package=1x01_offset]
  JP11 = Header 1 [package=1x01_offset]  # not connected
  JP12 = Header 1 [package=1x01_offset]
  JP13 = Header 1 [package=1x01_offset]  # not connected
  JP14 = Header 1 [package=1x01_offset]

nets:
  N1: Q1.E, JP1.1
  N2: R2.Pin_0, R3.Pin_1
  N3: R3.Pin_0, JP3.1
  N4: R4.Pin_0, JP4.1
  N5: R5.Pin_0, D2.A, JP6.1
  N6: R5.Pin_1, JP2.1
  N7: R6.Pin_0, R7.Pin_1
  N8: R7.Pin_0, JP10.1
  N9: R8.Pin_0, JP14.1
  N10: R9.Pin_0, D4.A, JP12.1
